# Fritzing sketch comprendre-encoder (saved by Fritzing 0.9.3b)

parts:
  Composant1 = Arduino Nano 33 IOT
  DC_Mot_Enc1 = DC Motor with two-phase hall-encoder [part_number=VT-E-G25A-06-177E]

nets:
  N1: Composant1.GND, Composant1.D13~, DC_Mot_Enc1.pin4
  N2: Composant1.D2, DC_Mot_Enc1.pin6
  N3: Composant1.D3~, DC_Mot_Enc1.pin5
  N4: Composant1.D11/MOSI, Composant1.+5V, DC_Mot_Enc1.pin3

custom parts:
  Arduino Nano 33 IOT: The Arduino Nano 33 IoT is the easiest and cheapest point of entry to enhance existing devices (and creating new ones) to be part of the IoT and designing pico-network applications. Whether you are looking at building a sensor network connected to your office or home router, or if you want to create a BLE device sending data to a cellphone, the Nano 33 IoT is your one-stop-solution for many of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
